// Digital circuit control.dig as structural Verilog
module control (
  input  sys,
  input  [4:0] op,
  input  clock,
  input  t_in,
  output [2:0] aluop,
  output T,
  output halt,
  output error,
  output jump
);

  wire and_1_out, and_2_out, and_3_out, halt_t, not_1_out, xor_1_out;

  and and_1 (and_1_out, ~op[3], op[4], ~sys);  // And
  and and_2 (and_2_out, op[1], op[2], ~op[3], ~op[4]);  // And
  and and_3 (and_3_out, op[2], ~op[3], ~op[4]);  // And
  and and_4 (halt_t, op[0], ~op[1], sys);  // And
  Register u_T (.D(t_in), .C(clock), .en(1'b1), .Q(T));
  Multiplexer #(.Bits(3)) multiplexer_1 (.sel(and_1_out), .in_0(3'b111), .in_1(op[2:0]), .out(aluop));
  xor xor_1 (xor_1_out, op[0], T);
  not not_1 (not_1_out, T);
  Multiplexer multiplexer_2 (.sel(and_2_out), .in_0(and_3_out), .in_1(xor_1_out), .out(jump));
  and and_5 (halt, T, halt_t);
  and and_6 (error, halt_t, not_1_out);
endmodule
