// Digital circuit decoder.dig as structural Verilog
module decoder (
  input  [31:0] instruction,
  output [15:0] A,
  output [1:0] rs,
  output [1:0] rd
);


  assign A = instruction[15:0];
  assign rd = instruction[17:16];
  assign rs = instruction[21:20];
endmodule
