// Digital circuit frontpanel.dig as structural Verilog
module frontpanel (
  input  [7:0] value,
  input  [1:0] dest,
  input  [1:0] src,
  input  tworeg,
  output [31:0] R0,
  output [31:0] R1,
  output [31:0] R2,
  output [31:0] R3,
  output [31:0] L,
  output [1:0] rs,
  output [1:0] rd,
  output [31:0] R,
  output [3:0] PC,
  output [31:0] target,
  output [1:0] rd_2,
  output [1:0] rs_2,
  output [1:0] rd_3,
  output [31:0] R_2
);

  wire add, add_out, advance_out, assembler_1_p10, decoder_1_p1, decoder_1_p2, decoder_1_p6, execute_1_p4,
       fetch_1_p8, hexdisplay_1_p1, hexdisplay_1_p2, hexdisplay_1_p3, hexdisplay_1_p4, hexdisplay_1_p5,
       hexdisplay_1_p6, hexdisplay_1_p7, hexdisplay_1_p8, hexdisplay_2_p1, hexdisplay_2_p2, hexdisplay_2_p3,
       hexdisplay_2_p4, hexdisplay_2_p5, hexdisplay_2_p6, hexdisplay_2_p7, hexdisplay_2_p8,
       instrdisplay_1_p3, instrdisplay_1_p5, instrdisplay_1_p7, instrdisplay_1_p9, instrdisplay_1_p11,
       instrdisplay_1_p13, jump, jump_out, mode_out, move, move_out, not_1_out, op, pmshim_1_c, pmshim_1_l,
       pmshim_1_s, regdisplay_1_p1, regdisplay_1_p2, regdisplay_2_p1, regdisplay_2_p2, tworeg_t;
  wire [3:0] hexdisplay_1_d1, hexdisplay_1_d2, hexdisplay_1_d3, hexdisplay_1_d4, hexdisplay_1_d5,
       hexdisplay_1_d6, hexdisplay_1_d7, hexdisplay_1_d8, hexdisplay_2_d1, hexdisplay_2_d2, hexdisplay_2_d3,
       hexdisplay_2_d4, hexdisplay_2_d5, hexdisplay_2_d6, hexdisplay_2_d7, hexdisplay_2_d8, pmshim_1_a;
  wire [15:0] assembler_1_p9, instrdisplay_1_p2, instrdisplay_1_p4, instrdisplay_1_p6, instrdisplay_1_p8,
       instrdisplay_1_p10, instrdisplay_1_p12, pmshim_1_d, Program_d, regdisplay_1_d1, regdisplay_1_d2,
       regdisplay_2_d1, regdisplay_2_d2;

  Button u_add (.out(add_out));
  Button u_move (.out(move_out));
  Button u_jump (.out(jump_out));
  LED programming (.in(mode_out));
  DipSwitch mode (.out(mode_out));
  SixteenSeg sixteenseg_1 (.led(regdisplay_1_d1), .dp(regdisplay_1_p1));
  SixteenSeg sixteenseg_2 (.led(regdisplay_1_d2), .dp(regdisplay_1_p2));
  regdisplay regdisplay_1 (
    .D1(regdisplay_1_d1), .P1(regdisplay_1_p1), .D2(regdisplay_1_d2), .P2(regdisplay_1_p2), .E(1'b1),
    .J(jump), .R(rd));
  // assembler assembler_1: pin names not known; wires that end beside it: mode_out, value, dest, src, tworeg, add_out, move_out, jump_out, assembler_1_p9, assembler_1_p10
  Seven_Seg_Hex seven_seg_hex_1 (.d(hexdisplay_1_d1), .dp(hexdisplay_1_p1));
  Seven_Seg_Hex seven_seg_hex_2 (.d(hexdisplay_1_d2), .dp(hexdisplay_1_p2));
  hexdisplay hexdisplay_1 (
    .D1(hexdisplay_1_d1), .P1(hexdisplay_1_p1), .D2(hexdisplay_1_d2), .P2(hexdisplay_1_p2),
    .D3(hexdisplay_1_d3), .P3(hexdisplay_1_p3), .D4(hexdisplay_1_d4), .P4(hexdisplay_1_p4),
    .D5(hexdisplay_1_d5), .P5(hexdisplay_1_p5), .D6(hexdisplay_1_d6), .P6(hexdisplay_1_p6),
    .D7(hexdisplay_1_d7), .P7(hexdisplay_1_p7), .D8(hexdisplay_1_d8), .P8(hexdisplay_1_p8), .E(not_1_out),
    .V(L));
  not not_1 (not_1_out, jump);
  pmshim pmshim_1 (
    .pc(PC), .i_in(assembler_1_p9), .s_c(assembler_1_p10), .A(pmshim_1_a), .D(pmshim_1_d), .s(pmshim_1_s),
    .C(pmshim_1_c), .L(pmshim_1_l));
  Seven_Seg_Hex seven_seg_hex_3 (.d(hexdisplay_1_d3), .dp(hexdisplay_1_p3));
  Seven_Seg_Hex seven_seg_hex_4 (.d(hexdisplay_1_d4), .dp(hexdisplay_1_p4));
  EEPROMDualPort #(.AddrBits(4), .isProgramMemory("true"), .Bits(16)) Program (
    .A(pmshim_1_a), .Din(pmshim_1_d), .str(pmshim_1_s), .C(pmshim_1_c), .ld(pmshim_1_l), .D(Program_d));
  Button advance (.out(advance_out));
  Seven_Seg_Hex seven_seg_hex_5 (.d(hexdisplay_1_d5), .dp(hexdisplay_1_p5));
  Seven_Seg_Hex seven_seg_hex_6 (.d(hexdisplay_1_d6), .dp(hexdisplay_1_p6));
  Seven_Seg_Hex seven_seg_hex_7 (.d(hexdisplay_1_d7), .dp(hexdisplay_1_p7));
  Seven_Seg_Hex seven_seg_hex_8 (.d(hexdisplay_1_d8), .dp(hexdisplay_1_p8));
  // fetch fetch_1: pin names not known; wires that end beside it: mode_out, assembler_1_p9, Program_d, advance_out, R, jump, PC, fetch_1_p8
  LED jump_2 (.in(jump));
  LED move_2 (.in(move));
  LED add_2 (.in(add));
  SixteenSeg sixteenseg_3 (.led(instrdisplay_1_p2), .dp(instrdisplay_1_p3));
  SixteenSeg sixteenseg_4 (.led(instrdisplay_1_p4), .dp(instrdisplay_1_p5));
  // instrdisplay instrdisplay_1: pin names not known; wires that end beside it: op, instrdisplay_1_p2, instrdisplay_1_p3, instrdisplay_1_p4, instrdisplay_1_p5, instrdisplay_1_p6, instrdisplay_1_p7, instrdisplay_1_p8, instrdisplay_1_p9, instrdisplay_1_p10, instrdisplay_1_p11, instrdisplay_1_p12, instrdisplay_1_p13
  // decoder decoder_1: pin names not known; wires that end beside it: decoder_1_p1, decoder_1_p2, fetch_1_p8, rs, rd, decoder_1_p6, L, R, tworeg_t, move, add, op, jump
  SixteenSeg sixteenseg_5 (.led(instrdisplay_1_p6), .dp(instrdisplay_1_p7));
  SixteenSeg sixteenseg_6 (.led(instrdisplay_1_p8), .dp(instrdisplay_1_p9));
  SixteenSeg sixteenseg_7 (.led(instrdisplay_1_p10), .dp(instrdisplay_1_p11));
  SixteenSeg sixteenseg_8 (.led(instrdisplay_1_p12), .dp(instrdisplay_1_p13));
  Seven_Seg_Hex seven_seg_hex_9 (.d(hexdisplay_2_d1), .dp(hexdisplay_2_p1));
  Seven_Seg_Hex seven_seg_hex_10 (.d(hexdisplay_2_d2), .dp(hexdisplay_2_p2));
  Seven_Seg_Hex seven_seg_hex_11 (.d(hexdisplay_2_d3), .dp(hexdisplay_2_p3));
  hexdisplay hexdisplay_2 (
    .D1(hexdisplay_2_d1), .P1(hexdisplay_2_p1), .D2(hexdisplay_2_d2), .P2(hexdisplay_2_p2),
    .D3(hexdisplay_2_d3), .P3(hexdisplay_2_p3), .D4(hexdisplay_2_d4), .P4(hexdisplay_2_p4),
    .D5(hexdisplay_2_d5), .P5(hexdisplay_2_p5), .D6(hexdisplay_2_d6), .P6(hexdisplay_2_p6),
    .D7(hexdisplay_2_d7), .P7(hexdisplay_2_p7), .D8(hexdisplay_2_d8), .P8(hexdisplay_2_p8), .E(1'b1), .V(R));
  // execute execute_1: pin names not known; wires that end beside it: decoder_1_p6, L, R, execute_1_p4
  Seven_Seg_Hex seven_seg_hex_12 (.d(hexdisplay_2_d4), .dp(hexdisplay_2_p4));
  Seven_Seg_Hex seven_seg_hex_13 (.d(hexdisplay_2_d5), .dp(hexdisplay_2_p5));
  Seven_Seg_Hex seven_seg_hex_14 (.d(hexdisplay_2_d6), .dp(hexdisplay_2_p6));
  Seven_Seg_Hex seven_seg_hex_15 (.d(hexdisplay_2_d7), .dp(hexdisplay_2_p7));
  // regfile regfile_1: pin names not known; wires that end beside it: rs, rd, execute_1_p4, advance_out, decoder_1_p1, decoder_1_p2, R0, R1, R2, R3
  Seven_Seg_Hex seven_seg_hex_16 (.d(hexdisplay_2_d8), .dp(hexdisplay_2_p8));
  SixteenSeg sixteenseg_9 (.led(regdisplay_2_d1), .dp(regdisplay_2_p1));
  regdisplay regdisplay_2 (
    .D1(regdisplay_2_d1), .P1(regdisplay_2_p1), .D2(regdisplay_2_d2), .P2(regdisplay_2_p2), .E(tworeg_t),
    .J(1'b0), .R(rs));
  SixteenSeg sixteenseg_10 (.led(regdisplay_2_d2), .dp(regdisplay_2_p2));

  assign R_2 = R;
  assign rd_2 = rd;
  assign rd_3 = rd;
  assign rs_2 = rs;
  assign target = R;

  // Notes on the sheet:
  //   rj45 Creates
  //   Fibonacci
  //   0: R2 = R2 + 1
  //   1: R2 = R2 + R1
  //   2: R3 = R2
  //   3: R1 = R1 + R2
  //   4: R3 = R1
  //   5: jump 1
  //   contents of Program (hex, n*v repeats v):
  //   120,161,1bd,191,17d,10e
  //   PC =
  //   R
  //   =
  //   ( R
  //   )
  //   +
endmodule
