// Digital circuit rj32.dig as structural Verilog
module rj32 (
  input  clock,
  input  step,
  input  run,
  input  [15:0] D_prog,
  input  [15:0] D_in,
  output [15:0] R0,
  output [15:0] R1,
  output [15:0] R2,
  output [15:0] R3,
  output [7:0] PC,
  output halt,
  output error,
  output skip,
  output rd_valid,
  output rs_valid,
  output [4:0] op,
  output [2:0] cond,
  output stall,
  output [15:0] L,
  output [15:0] R,
  output [1:0] rd,
  output [1:0] rs,
  output jump,
  output [7:0] A_prog,
  output clock_m,
  output [13:0] A_data,
  output [15:0] D_out,
  output w_en,
  output [15:0] result
);

  wire control_1_mem, control_1_memop, decoder_1_p2, en, execute_1_p6, fetch_1_p3, fetch_1_p7;
  wire [2:0] control_1_aluop;
  wire [15:0] decoder_1_p1, execute_1_p5;

  not not_1 (clock_m, clock);
  // fetch fetch_1: pin names not known; wires that end beside it: D_prog, clock, fetch_1_p3, jump, R, en, fetch_1_p7, A_prog
  // decoder decoder_1: pin names not known; wires that end beside it: decoder_1_p1, decoder_1_p2, fetch_1_p7, rs, rd, L, R, cond, op, rs_valid, rd_valid
  // clockctrl clockctrl_1: pin names not known; wires that end beside it: clock, step, run, stall
  control control_1 (
    .op(op), .stall(stall), .clock(clock), .skip_n(execute_1_p6), .aluop(control_1_aluop), .skip(skip),
    .halt(halt), .error(error), .en_write(en), .mem(control_1_mem), .memop(control_1_memop),
    .en_fetch(fetch_1_p3), .jump(jump));
  // execute execute_1: pin names not known; wires that end beside it: L, R, cond, control_1_aluop, execute_1_p5, execute_1_p6
  memaccess memaccess_1 (
    .result(execute_1_p5), .rdval(decoder_1_p1), .mem(control_1_mem), .store(control_1_memop), .D(D_in),
    .en(en), .wrval(result), .A(A_data), .str(w_en), .D_in(D_out));
  // regfile regfile_1: pin names not known; wires that end beside it: rs, rd, result, clock, en, decoder_1_p1, decoder_1_p2, R0, R1, R2, R3

  assign PC = A_prog;

  // Other names for the same wires on the sheet: A_data_t[13:0] = A_data; C = clock; cond_t[2:0] = cond;
  //   D_in_t[15:0] = D_in; D_out_t[15:0] = D_out; D_prog_t[15:0] = D_prog; error_t = error; halt_t = halt;
  //   jump_t = jump; L_t[15:0] = L; op_t[4:0] = op; A_prog_t[7:0] = A_prog; PC_t[7:0] = A_prog; R_t[15:0] = R;
  //   rd_t[1:0] = rd; rdvalid_t = rd_valid; result_t[15:0] = result; rs_t[1:0] = rs; rsvalid_t = rs_valid;
  //   skip_t = skip; stall_t = stall; W_en_t = w_en

  // Notes on the sheet:
  //   clock: Hz: 10
  //   rj45 Creates
endmodule
